# Fritzing sketch remote (saved by Fritzing 0.9.3b)
breadboards: 2
perfboards: 1

parts:
  Q1 = NPN-Transistor [package="TO92 [THT]"]
  Q2 = NPN-Transistor [package="TO92 [THT]"]
  Q3 = NPN-Transistor [package="TO92 [THT]"]
  S1 = Pushbutton [package="[THT]"]
  S2 = Pushbutton [package="[THT]"]
  S3 = Pushbutton [package="[THT]"]
  Part2 = Adafruit NeoPixel FeatherWing [part_number="Adafruit #2945"]
  LED1 = smd LED [color="Blue (430nm)" package="1206 [SMD]"]
  LED2 = smd LED [color="Yellow (595nm)" package="1206 [SMD]"]
  LED4 = smd LED [color="Green (555nm)" package="1206 [SMD]"]
  Part3 = Adafruit HUZZAH32 ESP32 Feather [part_number="Adafruit #3405"]

nets:
  N1: Q1.E, Q2.E, Q3.E, S1.Pin_1, S1.Pin_2, S2.Pin_1, S2.Pin_2, S3.Pin_1, S3.Pin_2, Part3.GND
  N2: Q1.B, LED4.anode
  N3: Q1.C, S2.Pin_3, S2.Pin_4
  N4: Q2.B, LED2.anode
  N5: Q2.C, S3.Pin_3, S3.Pin_4
  N6: Q3.B, LED1.anode
  N7: Q3.C, S1.Pin_3, S1.Pin_4
  N8: Part2.H, Part3.SCL
  N9: LED1.cathode, Part3.IO13_A12
  N10: LED2.cathode, Part3.IO33_A9
  N11: LED4.cathode, Part3.IO27_A10

notes:
  G- G+ 1 2 3 4 5 6 7 8 SH Y- Y+

custom parts:
  Adafruit NeoPixel FeatherWing: Put on your sunglasses before staring into these 32 configurable eye-blistering RGB LEDs. Arranged in a 4x8 matrix, each pixel is individually addressable. Only one pin is required to control all the LEDs. On the bottom we have jumpers for the DIN line to any of the I/O pins on a Feather. You can cut the default jumper trace and use any pin you like To make it easy to start, the LEDs are by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
